# Fritzing sketch LiveLights Core (saved by Fritzing 0.8.7b)

parts:
  Arduino1 = Arduino
  LPD8806_RGB_LED_Strip1 = LPD8806 RGB LED Strip
  LPD8806_RGB_LED_Strip2 = LPD8806 RGB LED Strip
  Power_plug2 = Power plug
  part = Power plug  # not connected

nets:
  N1: Arduino1.GND, LPD8806_RGB_LED_Strip1.GND#0
  N2: Arduino1.D13, LPD8806_RGB_LED_Strip1.DI
  N3: Arduino1.D11, LPD8806_RGB_LED_Strip1.CI
  GND: LPD8806_RGB_LED_Strip1.GND#4, LPD8806_RGB_LED_Strip2.GND, Power_plug2.GND
  N4: LPD8806_RGB_LED_Strip1.DO, LPD8806_RGB_LED_Strip2.DI
  N5: LPD8806_RGB_LED_Strip1.CO, LPD8806_RGB_LED_Strip2.CI
  +5V: LPD8806_RGB_LED_Strip1.+5V, LPD8806_RGB_LED_Strip2.+5V, Power_plug2.VCC

custom parts:
  LPD8806 RGB LED Strip: Digitally addressable RGB LED strip
